# Fritzing sketch WatchBot Model (saved by Fritzing 0.9.5d)
breadboards: 1

parts:
  R1 = Resistor [tolerance=±5% resistance=220 package="1206 [SMD]"]
  Brain = Raspberry Pi 5
  Suspisous_Person_Indicator = smd LED [color="Red (633nm)" package="0805 [SMD]"]
  R2 = Resistor [tolerance=±5% resistance=220 package="1206 [SMD]"]
  R3 = Resistor [tolerance=±5% resistance=220 package="1206 [SMD]"]
  S1 = Momentary Switch [package=ksa_sealed_tac_switch]
  part = LCD screen [part_number=Display]
  Buzzer = Piezo Speaker
  R4 = Resistor [tolerance=±5% resistance=1k package=THT]
  User_Related_Indicator = smd LED [color="Green (570nm)" package="0805 [SMD]"]

nets:
  GND: R1.Pin_0, Brain.GND, Suspisous_Person_Indicator.anode, S1.2, part.VSS, part.R/W, part.LED-, R4.Pin_1, User_Related_Indicator.cathode
  N1: R1.Pin_1, Buzzer.pin1
  5V: Brain.5V, part.VDD, part.LED+
  N2: Brain.GPIO14, S1.4
  N3: Brain.GPIO15, Buzzer.pin2
  N4: Brain.GPIO18, R2.Pin_0
  N5: Brain.GPIO24, part.DB7
  N6: Brain.GPIO25, part.DB6
  N7: Brain.GPIO8, part.DB5
  N8: Brain.GPIO7, part.DB4
  N9: Brain.GPIO5, part.E
  N10: Suspisous_Person_Indicator.cathode, R2.Pin_1
  N11: R3.Pin_0, User_Related_Indicator.anode
  N12: part.V0, R4.Pin_0

custom parts:
  Raspberry Pi 5: The RPi5, a faster version of the awesome Raspberry Pi4B ARM Board with 40 pin gpio.
